# Fritzing sketch gotasec (saved by Fritzing 0.9.3b)
breadboards: 1

parts:
  Part1 = Arduino Uno (Rev3) - ICSP
  Part2 = Adafruit Bluefruit LE UART Friend [part_number="Adafruit #2479"]
  R1 = Photocell (LDR) [package=THT]
  R2 = Resistor [tolerance=±5% resistance=10k package=THT]
  R3 = Resistor [tolerance=±5% resistance=220 package="2010 [SMD]"]
  LED1 = smd LED [color="Red (633nm)" package="0805 [SMD]"]

nets:
  N1: Part1.A0, R1.pin_0, R2.Pin_1
  N2: Part1.D8, Part2.RTS
  N3: Part1.D9_PWM, Part2.RXI
  N4: Part1.D10_PWM/SS, Part2.TXO
  N5: Part1.D11_PWM/MOSI, Part2.CTS
  N6: Part1.D12/MISO, Part2.MODE
  N7: Part1.D6_PWM, LED1.anode
  5V: Part1.5V, Part2.VIN, R1.pin_1
  GND: Part1.GND, Part2.GND, R2.Pin_0, R3.Pin_0
  N8: R3.Pin_1, LED1.cathode

custom parts:
  Adafruit Bluefruit LE UART Friend: The Bluefruit LE UART Friend makes it easy to add Bluetooth Low Energy connectivity to anything with a hardware or software serial port. We even have nice hardware flow control so you won't have to think about losing data. Connect to your Arduino or other microcontroller or even just a standard FTDI cable for debugging and testing.
